# Fritzing sketch esquema (saved by Fritzing 0.9.6b)

parts:
  부품2 = FC-28 Soil Hygrometer Module
  MCU1 = Wemos Lolin32lite
  LED3 = smd LED [color="White (4500K)" package="1206 [SMD]"]

nets:
  N1: 부품2.VCC, MCU1.pin_28
  N2: 부품2.GND, MCU1.pin_13
  N3: 부품2.DO, MCU1.pin_27
  N4: 부품2.POS, LED3.cathode
  N5: 부품2.NEG, LED3.anode

custom parts:
  FC-28 Soil Hygrometer Module: The FC-28 is a soil hygrometer module that uses the Texas Instruments LM393 comparator chip to provide an analog measurement of soil humidity. The digital output is high when soil moisture is over a certain threshold, as determined by adjusting the potentiometer.
  Wemos Lolin32lite: Wemos Lolinlite32 wifi and blue tooth board based on the ESP-32 cpu, digital I/Os 19, analog inputs 6, clock 240mhz, Flash 4Mbytes, lipo battery charger (500ma connection broken out on breadboard but not pcb), usb.
