# Fritzing sketch esquema (saved by Fritzing 0.9.6b)

parts:
  MCU1 = Wemos Lolin32lite
  JL012-13-5_1 = JL012-13-5.2 Lever (Limit) Switch SPDT + NO + NC [part_number=JL012-13-5.2]
  JL012-13-5_4 = JL012-13-5.2 Lever (Limit) Switch SPDT + NO + NC [part_number=JL012-13-5.2]
  JL012-13-5_5 = JL012-13-5.2 Lever (Limit) Switch SPDT + NO + NC [part_number=JL012-13-5.2]
  JL012-13-5_6 = JL012-13-5.2 Lever (Limit) Switch SPDT + NO + NC [part_number=JL012-13-5.2]
  JACK1 = 2.1mm Barrel Jack with Terminal Block
  U1 = 4-Channel 5v Relay Shield [package=relay-4ch5v10a]
  JACK2 = 2.1mm Barrel Jack with Terminal Block
  M1 = DC Motor
  M2 = DC Motor

nets:
  N1: MCU1.pin_6, JL012-13-5_4.NO
  N2: MCU1.pin_7, JL012-13-5_6.NO
  N3: MCU1.pin_8, JL012-13-5_4.NC, JL012-13-5_6.NC
  N4: MCU1.pin_9, JL012-13-5_5.NO
  N5: MCU1.pin_10, JL012-13-5_1.NO
  N6: MCU1.pin_11, JL012-13-5_1.NC, JL012-13-5_5.NC
  N7: MCU1.pin_13, U1.GND
  N8: MCU1.pin_24, U1.IN4
  N9: MCU1.pin_25, U1.IN3
  N10: MCU1.pin_26, U1.IN2
  N11: MCU1.pin_27, U1.IN1
  N12: MCU1.pin_28, U1.VCC
  N13: JACK1.POS, U1.K3-On, U1.K4-On
  N14: JACK1.NEG, U1.K3-In, U1.K4-In
  N15: U1.K1-In, U1.K2-In, JACK2.NEG
  N16: U1.K1-Off, M2.pin_1
  N17: U1.K1-On, U1.K2-On, JACK2.POS
  N18: U1.K2-Off, M2.pin_2
  N19: U1.K3-Off, M1.pin_1
  N20: U1.K4-Off, M1.pin_2

custom parts:
  Wemos Lolin32lite: Wemos Lolinlite32 wifi and blue tooth board based on the ESP-32 cpu, digital I/Os 19, analog inputs 6, clock 240mhz, Flash 4Mbytes, lipo battery charger (500ma connection broken out on breadboard but not pcb), usb.
  JL012-13-5.2 Lever (Limit) Switch SPDT + NO + NC: Micro Switch; Model No.: JL012-13.5-2; Actuator Action: Momentary; Actuator Type: Hinge Lever; Contact Configuration: 1NO, 1NC (SPDT) Temperature -25~65℃；Relative humidity: below 85%; Rate Voltage: 125V AC; Rated Current: 1A.
  4-Channel 5v Relay Shield: 4 Channel 5v Relay Shield w. 2x SPD-06VDC-SD-C
