# Fritzing sketch esquema (saved by Fritzing 0.9.6b)
breadboards: 1

parts:
  MCU1 = Wemos Lolin32lite
  RE1 = KY-040 Rotary encoder [package=THT]

nets:
  N1: MCU1.pin_8, RE1.SW
  N2: MCU1.pin_9, RE1.DT
  N3: MCU1.pin_10, RE1.CLK
  N4: MCU1.pin_13, RE1.GND
  N5: MCU1.pin_28, RE1.Vcc

custom parts:
  Wemos Lolin32lite: Wemos Lolinlite32 wifi and blue tooth board based on the ESP-32 cpu, digital I/Os 19, analog inputs 6, clock 240mhz, Flash 4Mbytes, lipo battery charger (500ma connection broken out on breadboard but not pcb), usb.
  KY-040 Rotary encoder: KY-040 Rotary Encoder with switch on breakout borad from AZ Delivery
