# Fritzing sketch esquema (saved by Fritzing 0.9.6b)
breadboards: 1

parts:
  L298N2 = L298N DC motor driver
  A1 = Esp32-c3 super mini
  JACK1 = 2.1mm Barrel Jack with Terminal Block
  LED1 = LED - 3mm [color="Infrared (850nm)" package="3 mm [THT]"]  # not connected
  LED2 = LED - 3mm [color="Infrared (850nm)" current=0.030 package="3 mm [THT]"]  # not connected
  LED3 = LED - 3mm [color="Infrared (850nm)" current=0.030 package="3 mm [THT]"]  # not connected

nets:
  N1: L298N2.12V, JACK1.POS
  N2: L298N2.GND, JACK1.NEG
  N3: L298N2.IN2, A1.Pin_8

custom parts:
  L298N DC motor driver: 2x DC motor driver with 78M05 positive voltage regulator (7..35 V) L298N: max 46 V, 2 A Set 5 V Enable jumper to enable 5 V regultor (needed for the L298N) and +5 V output at screw terminal or supply external +5 V at screw terminal Set ENA and/or ENB to +5 V to enable motor permanently or supply ENA and/or ENB with PWM signal IN1 and IN2 set rotation directory for motor A (OUT1/OUT2) IN2 and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
  Esp32-c3 super mini: ESP32-C3 Development Board ESP32 SuperMini Development Board ESP32 Development Board WiFi Bluetooth.
