# Fritzing sketch esquema (saved by Fritzing 0.9.6b)
breadboards: 1

parts:
  R1 = Temperature Sensor (Thermistor) [thermistor_type=NTC package=THT]
  R2 = Resistor [tolerance=±5% resistance=220 package="1206 [SMD]"]
  MCU1 = Wemos Lolin32lite

nets:
  N1: R1.pin_0, R2.Pin_1, MCU1.pin_7
  N2: R1.pin_1, MCU1.pin_6
  N3: R2.Pin_0, MCU1.pin_13

custom parts:
  Wemos Lolin32lite: Wemos Lolinlite32 wifi and blue tooth board based on the ESP-32 cpu, digital I/Os 19, analog inputs 6, clock 240mhz, Flash 4Mbytes, lipo battery charger (500ma connection broken out on breadboard but not pcb), usb.
