# Fritzing sketch esquema (saved by Fritzing 0.9.6b)
breadboards: 1

parts:
  R1 = Photocell (LDR) [package=THT]
  MCU1 = Wemos Lolin32lite
  U1 = POT [package=pot_alpha_rv16af-20]
  R4 = Resistor [tolerance=±5% resistance=220 package="0805 [SMD]"]
  R5 = Resistor [tolerance=±5% resistance=220 package="0805 [SMD]"]

nets:
  N1: R1.pin_0, MCU1.pin_7, R4.Pin_1
  N2: R1.pin_1, MCU1.pin_28, U1.A
  N3: MCU1.pin_5, U1.S, R5.Pin_1
  N4: R4.Pin_0, R5.Pin_0

custom parts:
  Wemos Lolin32lite: Wemos Lolinlite32 wifi and blue tooth board based on the ESP-32 cpu, digital I/Os 19, analog inputs 6, clock 240mhz, Flash 4Mbytes, lipo battery charger (500ma connection broken out on breadboard but not pcb), usb.
