# Fritzing sketch esquema (saved by Fritzing 0.9.6b)
breadboards: 1

parts:
  U1 = Wemos Lolin D32
  DS1 = DS18B20 1-Wire Temperature Sensor Probe
  R1 = Resistor [tolerance=±5% resistance=220 package="0402 [SMD]"]
  A1 = tds-sensor-meter-v1.0_1

nets:
  N1: U1.pin_6, A1.pin1
  N2: U1.pin_18, U1.pin_33
  N3: U1.pin_26, DS1.DQ, R1.Pin_0
  N4: DS1.GND, A1.pin3
  N5: DS1.VDD, R1.Pin_1, A1.pin2

custom parts:
  Wemos Lolin D32: Wemos Lolin D32 wifi and blue tooth board based on the ESP-32 cpu, digital I/Os 22, analog inputs 6, analog outputs 2 clock 240mhz, Flash 4Mbytes, lipo battery charger (500ma connection broken out on breadboard but not pcb), usb. The mounting holes are only set on the silkscreen, if you want actual holes in the pcb copy the hole from the pcb menu in parts over the top of the hole in the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
  : TDS Meter V1.0 Development Board Water Meter Filter Measuring Water Sensor Module.
