# Fritzing sketch esquema (saved by Fritzing 0.9.6b)
breadboards: 1

parts:
  DS1 = DS18B20 1-Wire Temperature Sensor Probe  # not connected
  MCU1 = Wemos Lolin32lite
  DS2 = DS18B20 1-Wire Temperature Sensor Probe
  R1 = Resistor [tolerance=±5% resistance=4.7k package="2512 [SMD]"]

nets:
  N1: MCU1.pin_24, R1.Pin_1
  N2: MCU1.pin_28, DS2.VDD, R1.Pin_0

custom parts:
  Wemos Lolin32lite: Wemos Lolinlite32 wifi and blue tooth board based on the ESP-32 cpu, digital I/Os 19, analog inputs 6, clock 240mhz, Flash 4Mbytes, lipo battery charger (500ma connection broken out on breadboard but not pcb), usb.
