# Fritzing sketch esquema (saved by Fritzing 0.9.6b)
breadboards: 1

parts:
  MCU1 = Wemos Lolin32lite
  DS2 = DS18B20 1-Wire Temperature Sensor Probe
  R1 = Resistor [tolerance=±5% resistance=4.7k package="2512 [SMD]"]
  Mod1 = KY-019 5V Relay Module [package="Breakout board"]
  JACK1 = 2.1mm Barrel Jack with Terminal Block
  L1 = Inductor [package="1206 [SMD]"]

nets:
  N1: MCU1.pin_8, Mod1.S
  N2: MCU1.pin_9, DS2.DQ, R1.Pin_1
  N3: MCU1.pin_13, DS2.GND, Mod1.-
  N4: MCU1.pin_28, DS2.VDD, R1.Pin_0, Mod1.+
  N5: Mod1.Common, L1.pin_1
  N6: Mod1.NO, JACK1.NEG
  N7: JACK1.POS, L1.pin_0

custom parts:
  Wemos Lolin32lite: Wemos Lolinlite32 wifi and blue tooth board based on the ESP-32 cpu, digital I/Os 19, analog inputs 6, clock 240mhz, Flash 4Mbytes, lipo battery charger (500ma connection broken out on breadboard but not pcb), usb.
  KY-019 5V Relay Module: KY-019 5V Relay module, used to control AC circuits. (Special thanks to vanepp for fixing the PCB holes and other errors)
